// Logisim project 4bits-adder-bits-data.circ as structural Verilog: 1 circuit, main circuit main
module main (
  input  in_1,
  input  [3:0] A___4bit_number,
  input  [3:0] B_4bit_number,
  output [3:0] out_4,
  output out_5
);

  wire adder_1_cout, adder_2_cout, adder_3_cout, adder_4_cout, undriven;

  Adder #(.width(1)) adder_1 (
    .a(A___4bit_number[0]), .b(B_4bit_number[0]), .out(out_4[0]), .cin(undriven), .cout(adder_1_cout));
  Adder #(.width(1)) adder_2 (
    .a(A___4bit_number[1]), .b(B_4bit_number[1]), .out(out_4[1]), .cin(adder_1_cout), .cout(adder_2_cout));
  Adder #(.width(1)) adder_3 (
    .a(A___4bit_number[2]), .b(B_4bit_number[2]), .out(out_4[2]), .cin(adder_2_cout), .cout(adder_3_cout));
  Adder #(.width(1)) adder_4 (
    .a(A___4bit_number[3]), .b(B_4bit_number[3]), .out(out_4[3]), .cin(adder_3_cout), .cout(adder_4_cout));

  // Notes on the sheet:
  //   4 bit adder with bits numbers
endmodule
