// Logisim project full-adder.circ as structural Verilog: 1 circuit, main circuit Cont
module Cont (
  input  [3:0] in_1,
  input  carry,
  input  [3:0] in_3,
  output [3:0] out_4,
  output out_5
);

  wire and_1_out, and_2_out, and_3_out, and_4_out, and_5_out, and_6_out, and_7_out, and_8_out, or_1_out,
       or_2_out, or_3_out, xor_1_out, xor_2_out, xor_3_out, xor_4_out;

  xor xor_1 (xor_1_out, in_1[0], in_3[0]);
  and and_1 (and_1_out, in_1[0], in_3[0]);
  xor xor_2 (xor_2_out, in_1[1], in_3[1]);
  and and_2 (and_2_out, in_1[1], in_3[1]);
  xor xor_3 (xor_3_out, in_1[2], in_3[2]);
  and and_3 (and_3_out, in_1[2], in_3[2]);
  xor xor_4 (xor_4_out, in_1[3], in_3[3]);
  and and_4 (and_4_out, in_1[3], in_3[3]);
  and and_5 (and_5_out, xor_1_out, carry);
  xor xor_5 (out_4[0], xor_1_out, carry);
  xor xor_6 (out_4[1], xor_2_out, or_1_out);
  and and_6 (and_6_out, xor_2_out, or_1_out);
  xor xor_7 (out_4[2], xor_3_out, or_2_out);
  and and_7 (and_7_out, xor_3_out, or_2_out);
  xor xor_8 (out_4[3], xor_4_out, or_3_out);
  and and_8 (and_8_out, xor_4_out, or_3_out);
  or or_1 (or_1_out, and_5_out, and_1_out);
  or or_2 (or_2_out, and_6_out, and_2_out);
  or or_3 (or_3_out, and_7_out, and_3_out);
  or or_4 (out_5, and_8_out, and_4_out);

  // Notes on the sheet:
  //   a
  //   b
  //   a
  //   b
  //   carry
  //   a
  //   b
  //   carry
  //   Full adder
  //   a
  //   b
  //   carry
  //   carry
  //   carry
  //   carry
  //   sum
  //   sum
  //   sum
  //   sum
  //   overflow
  //   truth table
  //   1011 a
  //   0010 b
  //   ----------
  //   1101
endmodule
